// Logisim project ARM_Processor_Single_Cycle.circ as structural Verilog: 2 circuits, main circuit ARM_Processor_Single_Cycle
module ARM_Processor_Single_Cycle (
  input  PCWrite
);

  wire CLK, Control_Unit_p6, Control_Unit_p8, Control_Unit_p9, Control_Unit_p10, Control_Unit_p11,
       Control_Unit_p12, Control_Unit_p13, PCSrc, Registers_p8;
  wire [1:0] Control_Unit_p14;
  wire [3:0] multiplexer_2_out, multiplexer_3_out;
  wire [7:0] ALU_p5_2;
  wire [31:0] adder_1_out, adder_2_out, ALU_p5, Data_dout, Extend_p3, Instructions_data, multiplexer_1_out,
       multiplexer_4_out, PC_q, Registers_p4, Registers_p9, Shift_y;

  // Probe on multiplexer_1_out
  Multiplexer #(.width(32)) multiplexer_1 (.in0(adder_1_out), .in1(Registers_p4), .out(multiplexer_1_out), .sel(PCSrc));
  Register #(.width(32)) PC (.D(multiplexer_1_out), .en(PCWrite), .clk(CLK), .Q(PC_q));  // open: clr
  Clock u_CLK (.out(CLK));
  // Probe on PC_q[9:2]
  ROM #(.dataWidth(32)) Instructions (.addr(PC_q[9:2]), .data(Instructions_data));
  Adder #(.width(32)) adder_1 (.a(PC_q), .b(32'h4), .out(adder_1_out));  // open: cin, cout
  // Probe on Instructions_data
  Adder #(.width(32)) adder_2 (.a(32'h4), .b(adder_1_out), .out(adder_2_out));  // open: cin, cout
  Multiplexer #(.width(4)) multiplexer_2 (
    .in0(Instructions_data[19:16]), .in1(4'b1111), .out(multiplexer_2_out), .sel(Control_Unit_p14[0]));
  Multiplexer #(.width(4)) multiplexer_3 (
    .in0(Instructions_data[3:0]), .in1(Instructions_data[15:12]), .out(multiplexer_3_out),
    .sel(Control_Unit_p14[1]));
  // ARM_Control_Unit Control_Unit: pin names not known; wires that end beside it: CLK, Instructions_data[31:28], Instructions_data[27:26], Instructions_data[25:20], Instructions_data[15:12], Control_Unit_p6, PCSrc, Control_Unit_p8, Control_Unit_p9, Control_Unit_p10, Control_Unit_p11, Control_Unit_p12, Control_Unit_p13, Control_Unit_p14
  // RegisterFile Registers: pin names not known; wires that end beside it: multiplexer_2_out, multiplexer_3_out, Instructions_data[15:12], Registers_p4, adder_2_out, CLK, Control_Unit_p13, Registers_p8, Registers_p9
  // ARM_Extend Extend: pin names not known; wires that end beside it: Instructions_data[23:0], Control_Unit_p12, Extend_p3
  Multiplexer #(.width(32)) multiplexer_4 (
    .in0(Shift_y), .in1(Extend_p3), .out(multiplexer_4_out), .sel(Control_Unit_p11));
  ARM_Shifter Shift (.X(Registers_p9), .ctl(Instructions_data[11:5]), .Y(Shift_y));
  // ALU_32_bit ALU: pin names not known; wires that end beside it: Registers_p8, multiplexer_4_out, Control_Unit_p10, Control_Unit_p6, {ALU_p5[31:10], ALU_p5_2, ALU_p5[1:0]}
  RAM #(.dataWidth(32), .enables("line"), .\type ("nonvolatile")) Data (
    .addr(ALU_p5_2), .we(Control_Unit_p9), .clk(CLK), .din(Registers_p9), .dout(Data_dout));
  // Probe on {ALU_p5[31:10], ALU_p5_2, ALU_p5[1:0]}
  // Probe on Registers_p4
  // Probe on Data_dout
  Multiplexer #(.width(32)) multiplexer_5 (
    .in0({ALU_p5[31:10], ALU_p5_2, ALU_p5[1:0]}), .in1(Data_dout), .out(Registers_p4), .sel(Control_Unit_p8));

  // Notes on the sheet:
  //   PCWrite: initial=0x1
  //   contents of Instructions (hex, n*v repeats v):
  //   e04f000f e2802005 e280300c e2437009 e1874002 e0035004 e0855004 e0558007 a00000c e0538004 aa000000
  //   e2805000 e0578002 b2857001 e0477002 e5837054 e5902060 e08ff000 e280200e ea000001 e280200d e280200a
  //   e5802064
  //   PCPlus4
  //   Memory units use 8-bit addresses to make things easier for now. Make sure PC doesn't go above that.
  //   PCPlus8
  //   They also use word addressing instead of byte-addressing so constants the last 2 LSBs of the 32-bit byte addresses are dropped at the address inputs on the memory units.
endmodule

module ARM_Shifter (
  input  [6:0] ctl,
  input  [31:0] X,
  output [31:0] Y
);

  // Probe on ctl[6:2]
  // Probe on ctl[1:0]

  assign Y = X;

  // Notes on the sheet:
  //   sh selects the different shift operation
  //   00 = LSL = Logical left shift
  //   01 = LSR = Logical right shift
  //   10 = ASR = Arithmetic shift right
  //   11 = ROR = Rotate right
  //   TODO: Implement this in VHDL as a 32-bit shifter is quite tedious to implement visually.
endmodule
