// Logisim project xetroc.circ as structural Verilog: 25 circuits, main circuit main
module main (
);

  wire clk_out, clock_1_out, clock_2_out, Control_Unit1_alusrc, Control_Unit1_memtoreg,
       Control_Unit1_memwrite, Control_Unit1_pcsrc, Control_Unit1_regwrite, por_1_out;
  wire [1:0] Control_Unit1_immsrc, Control_Unit1_regsrc;
  wire [2:0] Control_Unit1_alucontrol, multiplexer_2_out, multiplexer_3_out, multiplexer_4_out;
  wire [2:2] Control_Unit1_regsrc_2;
  wire [3:0] ALU1_aluflags;
  wire [15:0] ROM1_data;
  wire [31:0] adder_1_out, adder_2_out, ALU1_result, Immediate1_imm32, multiplexer_1_out, multiplexer_5_out,
       multiplexer_6_out, PC_q, RAM1_dout, RegisterFile1_rd1, RegisterFile1_rd2;

  Clock clk (.out(clk_out));
  LED led_1 (.in(clk_out));
  Register #(.width(32)) PC (.D(multiplexer_1_out), .en(1'b1), .clk(clock_1_out), .Q(PC_q), .clr(por_1_out));
  Multiplexer #(.width(32)) multiplexer_1 (
    .in0(adder_1_out), .in1(multiplexer_6_out), .out(multiplexer_1_out), .sel(Control_Unit1_pcsrc));
  Clock clock_1 (.out(clock_1_out));
  POR #(.PorHighDuration(1), .porsize(1)) por_1 (.out(por_1_out));
  ROM #(.addrWidth(16), .dataWidth(16)) ROM1 (.addr(PC_q[16:1]), .data(ROM1_data));
  Adder #(.width(32)) adder_1 (.a(PC_q), .b(32'h2), .out(adder_1_out));  // open: cin, cout
  // Probe on Control_Unit1_pcsrc
  // Probe on adder_1_out
  // Probe on ROM1_data
  // Probe on Control_Unit1_regsrc_2[2]
  // Probe on multiplexer_2_out
  Multiplexer #(.width(3)) multiplexer_2 (
    .in0(ROM1_data[5:3]), .in1(ROM1_data[10:8]), .out(multiplexer_2_out), .sel(Control_Unit1_regsrc_2[2]));
  // Probe on multiplexer_3_out
  Multiplexer #(.width(3)) multiplexer_3 (
    .in0(ROM1_data[8:6]), .in1(ROM1_data[10:8]), .out(multiplexer_3_out), .sel(Control_Unit1_regsrc_2[2]));
  // Probe on multiplexer_4_out
  Multiplexer #(.width(3)) multiplexer_4 (
    .in0(ROM1_data[2:0]), .in1(ROM1_data[10:8]), .out(multiplexer_4_out), .sel(Control_Unit1_regsrc_2[2]));
  Adder #(.width(32)) adder_2 (.a(adder_1_out), .b(32'h2), .out(adder_2_out));  // open: cin, cout
  Control_Unit Control_Unit1 (
    .Instr(ROM1_data), .ALUFlags(ALU1_aluflags), .MemToReg(Control_Unit1_memtoreg),
    .MemWrite(Control_Unit1_memwrite), .ALUControl(Control_Unit1_alucontrol), .ALUSrc(Control_Unit1_alusrc),
    .ImmSrc(Control_Unit1_immsrc), .RegWrite(Control_Unit1_regwrite),
    .RegSrc({Control_Unit1_regsrc_2[2], Control_Unit1_regsrc}), .PCSrc(Control_Unit1_pcsrc));
  // Probe on Control_Unit1_regwrite
  // Probe on adder_2_out
  // Probe on Control_Unit1_immsrc
  // Probe on Control_Unit1_regsrc
  RegisterFile RegisterFile1 (
    .WE3(Control_Unit1_regwrite), .SP_PC(Control_Unit1_regsrc), .A2(multiplexer_3_out),
    .A3(multiplexer_4_out), .A1(multiplexer_2_out), .R15(adder_2_out), .WD3(multiplexer_6_out),
    .RD1(RegisterFile1_rd1), .RD2(RegisterFile1_rd2));
  Immediate Immediate1 (.ImmSrc(Control_Unit1_immsrc), .Instr(ROM1_data), .Imm32(Immediate1_imm32));
  // Probe on Control_Unit1_alusrc
  Multiplexer #(.width(32)) multiplexer_5 (
    .in0(RegisterFile1_rd2), .in1(Immediate1_imm32), .out(multiplexer_5_out), .sel(Control_Unit1_alusrc));
  // Probe on Immediate1_imm32
  // Probe on Control_Unit1_alucontrol
  // Probe on RegisterFile1_rd1
  // Probe on multiplexer_5_out
  // Probe on RegisterFile1_rd2
  // Probe on ALU1_aluflags
  ALU ALU1 (
    .A(RegisterFile1_rd1), .B(multiplexer_5_out), .ALUControl(Control_Unit1_alucontrol),
    .Result(ALU1_result), .ALUFlags(ALU1_aluflags));
  // Probe on Control_Unit1_memwrite
  RAM #(.addrWidth(16), .asyncread("true"), .dataWidth(32)) RAM1 (
    .addr(ALU1_result[17:2]), .we(Control_Unit1_memwrite), .oe(Control_Unit1_memtoreg), .clk(clock_2_out),
    .din(RegisterFile1_rd2), .dout(RAM1_dout));
  Clock clock_2 (.out(clock_2_out));
  // Probe on ALU1_result
  // Probe on multiplexer_6_out
  // Probe on Control_Unit1_memtoreg
  // Probe on RAM1_dout
  Multiplexer #(.width(32)) multiplexer_6 (
    .in0(ALU1_result), .in1(RAM1_dout), .out(multiplexer_6_out), .sel(Control_Unit1_memtoreg));

  // Notes on the sheet:
  //   contents of ROM1 (hex, n*v repeats v):
  //   20ee 2193 1a0a d005 1a42 d801 1a09 e7f9 1a40 e7f7 e7fe
  //   NZCV
endmodule

module RegisterFile (
  input  [1:0] SP_PC,
  input  [2:0] A1,
  input  [2:0] A2,
  input  [2:0] A3,
  input  WE3,
  input  [31:0] WD3,
  input  [31:0] R15,
  output [31:0] RD1,
  output [31:0] RD2
);

  wire clock_1_out, decoder_1_out0, decoder_1_out1, decoder_1_out2, decoder_1_out3, decoder_1_out4,
       decoder_1_out5, decoder_1_out6, decoder_1_out7;
  wire [3:0] multiplexer_1_out;
  wire [31:0] R0_q, R1_q, R2_q, R3_q, R4_q, R5_q, R6_q, R7_q;

  Clock clock_1 (.out(clock_1_out));
  // Probe on A3
  Decoder #(.select(3)) decoder_1 (
    .out0(decoder_1_out0), .out1(decoder_1_out1), .out2(decoder_1_out2), .out3(decoder_1_out3),
    .out4(decoder_1_out4), .out5(decoder_1_out5), .out6(decoder_1_out6), .out7(decoder_1_out7), .sel(A3),
    .en(WE3));
  Multiplexer #(.select(2), .width(4)) multiplexer_1 (
    .in0({1'b0, A1}), .in1(4'b1111), .in2(4'b1101), .out(multiplexer_1_out), .sel(SP_PC));  // open: in3
  Register #(.width(32)) R0 (.D(WD3), .en(decoder_1_out0), .clk(clock_1_out), .Q(R0_q));  // open: clr
  Register #(.width(32)) R1 (.D(WD3), .en(decoder_1_out1), .clk(clock_1_out), .Q(R1_q));  // open: clr
  Register #(.width(32)) R2 (.D(WD3), .en(decoder_1_out2), .clk(clock_1_out), .Q(R2_q));  // open: clr
  Register #(.width(32)) R3 (.D(WD3), .en(decoder_1_out3), .clk(clock_1_out), .Q(R3_q));  // open: clr
  Register #(.width(32)) R4 (.D(WD3), .en(decoder_1_out4), .clk(clock_1_out), .Q(R4_q));  // open: clr
  Register #(.width(32)) R5 (.D(WD3), .en(decoder_1_out5), .clk(clock_1_out), .Q(R5_q));  // open: clr
  Register #(.width(32)) R6 (.D(WD3), .en(decoder_1_out6), .clk(clock_1_out), .Q(R6_q));  // open: clr
  Register #(.width(32)) R7 (.D(WD3), .en(decoder_1_out7), .clk(clock_1_out), .Q(R7_q));  // open: clr
  // Probe on A2
  Multiplexer #(.select(3), .width(32)) multiplexer_2 (
    .in0(R0_q), .in1(R1_q), .in2(R2_q), .in3(R3_q), .in4(R4_q), .in5(R5_q), .in6(R6_q), .in7(R7_q),
    .out(RD2), .sel(A2));
  // Probe on multiplexer_1_out
  Multiplexer #(.select(4), .width(32)) multiplexer_3 (
    .in0(R0_q), .in1(R1_q), .in2(R2_q), .in3(R3_q), .in4(R4_q), .in5(R5_q), .in6(R6_q), .in7(R7_q),
    .in13(32'h20000000), .in15(R15), .out(RD1), .sel(multiplexer_1_out));  // open: in8, in9, in10, in11, in12, in14

  // Notes on the sheet:
  //   PC
  //   SP
  //   SP
  //   PC
endmodule

module ALU (
  input  [2:0] ALUControl,
  input  [31:0] A,
  input  [31:0] B,
  output [31:0] Result,
  output [3:0] ALUFlags
);

  wire Adder_carryout, not_2_out, Sum31, xnor_1_out, xor_1_out;
  wire [30:0] Adder_sum;
  wire [31:0] and_1_out, multiplexer_1_out, multiplexer_2_out, not_1_out, or_1_out;

  Multiplexer #(.width(32)) multiplexer_1 (.in0({32{1'b0}}), .in1(A), .out(multiplexer_1_out), .sel(ALUControl[2]));
  assign not_1_out = ~B;  // NOT_Gate not_1, 32 bits wide
  Multiplexer #(.width(32)) multiplexer_2 (.in0(B), .in1(not_1_out), .out(multiplexer_2_out), .sel(ALUControl[0]));
  assign and_1_out = B & multiplexer_1_out;  // AND_Gate and_1, 32 bits wide
  assign or_1_out = B | multiplexer_1_out;  // OR_Gate or_1, 32 bits wide
  xor xor_1 (xor_1_out, Sum31, multiplexer_1_out[31]);
  NotExactlyOne xnor_1 (.out(xnor_1_out), .in0(multiplexer_1_out[31]), .in1(B[31]), .in2(ALUControl[0]));
  Adder_32_bit Adder (
    .A(multiplexer_1_out), .B(multiplexer_2_out), .CarryIn(ALUControl[0]), .CarryOut(Adder_carryout),
    .Sum({Sum31, Adder_sum}));
  not not_2 (not_2_out, ALUControl[1]);
  Multiplexer #(.select(3), .width(32)) multiplexer_3 (
    .in0({Sum31, Adder_sum}), .in1({Sum31, Adder_sum}), .in2({32{1'b0}}), .in3(A), .in4({Sum31, Adder_sum}),
    .in5({Sum31, Adder_sum}), .in6(and_1_out), .in7(or_1_out), .out({ALUFlags[3], Result[30:0]}),
    .sel(ALUControl));
  and and_2 (ALUFlags[1], Adder_carryout, not_2_out);
  and and_3 (ALUFlags[0], not_2_out, xor_1_out, xnor_1_out);
  Zero_Detect_32_bit Zero_Detect (.A({ALUFlags[3], Result[30:0]}), .B(ALUFlags[2]));

  assign Result[31] = ALUFlags[3];

  // Notes on the sheet:
  //   000 B
  //   001 -B
  //   010 0
  //   011 A
  //   100 A + B
  //   101 A - B
  //   110 A & B
  //   111 A | B
  //   Negative
  //   Carry
  //   oVerflow
  //   Zero
  //   NZCV
endmodule

module Immediate (
  input  [1:0] ImmSrc,
  input  [15:0] Instr,
  output [31:0] Imm32
);

  wire [29:0] bit_extender_2_out;
  wire [30:0] bit_extender_3_out, bit_extender_4_out;
  wire [31:0] bit_extender_1_out;

  assign bit_extender_1_out = {{24{1'b0}}, Instr[7:0]};  // Bit_Extender bit_extender_1
  assign bit_extender_2_out = {{22{1'b0}}, Instr[7:0]};  // Bit_Extender bit_extender_2
  assign bit_extender_3_out = {{23{Instr[7]}}, Instr[7:0]};  // Bit_Extender bit_extender_3
  assign bit_extender_4_out = {{20{Instr[10]}}, Instr[10:0]};  // Bit_Extender bit_extender_4
  Multiplexer #(.select(2), .width(32)) multiplexer_1 (
    .in0(bit_extender_1_out), .in1({bit_extender_2_out, 2'b00}), .in2({bit_extender_3_out, 1'b0}),
    .in3({bit_extender_4_out, 1'b0}), .out(Imm32), .sel(ImmSrc));

  // Notes on the sheet:
  //   00: imm8
  //   01: imm8 << 2
  //   10: simm8 << 1
  //   11: simm11 << 1
endmodule

module Condition_Check (
  input  [3:0] Cond,
  input  [3:0] ALUFlags,
  output CondEx
);

  wire and_1_out, and_2_out, not_1_out, not_2_out, not_3_out, not_4_out, not_5_out, not_6_out, not_7_out,
       xor_1_out;

  xor xor_1 (xor_1_out, ALUFlags[3], ALUFlags[0]);
  and and_1 (and_1_out, ~ALUFlags[2], ALUFlags[1]);  // AND_Gate
  not not_1 (not_1_out, xor_1_out);
  and and_2 (and_2_out, not_1_out, ~ALUFlags[2]);  // AND_Gate
  not not_2 (not_2_out, ALUFlags[2]);
  not not_3 (not_3_out, ALUFlags[1]);
  not not_4 (not_4_out, ALUFlags[3]);
  not not_5 (not_5_out, ALUFlags[0]);
  not not_6 (not_6_out, and_1_out);
  not not_7 (not_7_out, and_2_out);
  Multiplexer #(.select(4)) multiplexer_1 (
    .in0(ALUFlags[2]), .in1(not_2_out), .in2(ALUFlags[1]), .in3(not_3_out), .in4(ALUFlags[3]),
    .in5(not_4_out), .in6(ALUFlags[0]), .in7(not_5_out), .in8(and_1_out), .in9(not_6_out), .in10(not_1_out),
    .in11(xor_1_out), .in12(and_2_out), .in13(not_7_out), .in14(1'b1), .out(CondEx), .sel(Cond));  // open: in15

  // Other names for the same wires on the sheet: V = ALUFlags[0]; C = ALUFlags[1]; Z = ALUFlags[2]; N = ALUFlags[3]

  // Notes on the sheet:
  //   Negative
  //   Zero
  //   Carry
  //   oVerflow
endmodule

module Conditional_Logic (
  input  [3:0] ALUFlags,
  input  [1:0] FlagW,
  input  [3:0] Cond,
  input  MemW,
  input  RegW,
  input  PCS,
  output PCSrc,
  output RegWrite,
  output MemWrite
);

  wire and_1_out, and_2_out, clock_1_out, Condition_Check1_condex;
  wire [1:0] Flags_CV_q, Flags_NZ_q;

  Clock clock_1 (.out(clock_1_out));
  and and_1 (and_1_out, FlagW[1], Condition_Check1_condex);
  and and_2 (and_2_out, FlagW[0], Condition_Check1_condex);
  Register #(.width(2)) Flags_NZ (.D(ALUFlags[3:2]), .en(and_1_out), .clk(clock_1_out), .Q(Flags_NZ_q));  // open: clr
  Register #(.width(2)) Flags_CV (.D(ALUFlags[1:0]), .en(and_2_out), .clk(clock_1_out), .Q(Flags_CV_q));  // open: clr
  LED N (.in(Flags_NZ_q[1]));
  LED Z (.in(Flags_NZ_q[0]));
  LED C (.in(Flags_CV_q[1]));
  LED V (.in(Flags_CV_q[0]));
  Condition_Check Condition_Check1 (.Cond(Cond), .ALUFlags({Flags_NZ_q, Flags_CV_q}), .CondEx(Condition_Check1_condex));
  and and_3 (PCSrc, PCS, Condition_Check1_condex);
  and and_4 (RegWrite, RegW, Condition_Check1_condex);
  and and_5 (MemWrite, MemW, Condition_Check1_condex);

  // Other names for the same wires on the sheet: ALUFlagsCV[1:0] = ALUFlags[1:0]; ALUFlagsNZ[1:0] = ALUFlags[3:2]
endmodule

module Instruction_Decoder (
  input  [9:0] Opcode,
  output \always ,
  output PCS,
  output MemToReg,
  output MemW,
  output ALUSrc,
  output [1:0] ImmSrc,
  output RegW,
  output [2:0] RegSrc,
  output [2:0] ALUControl,
  output [1:0] FlagW
);

  wire and_3_out, and_4_out, and_5_out, and_6_out, and_7_out, and_10_out, and_11_out, and_12_out, not_2_out,
       not_3_out, not_4_out, not_5_out;

  not not_1 (FlagW[1], Opcode[9]);
  not not_2 (not_2_out, Opcode[8]);
  not not_3 (not_3_out, Opcode[7]);
  not not_4 (not_4_out, Opcode[6]);
  not not_5 (not_5_out, Opcode[5]);
  or or_1 (\always , not_2_out, not_4_out);
  and and_1 (MemToReg, Opcode[9], not_2_out, Opcode[5]);
  and and_2 (MemW, Opcode[9], not_2_out, not_5_out);
  or or_2 (ALUSrc, Opcode[9], Opcode[7]);
  and and_3 (and_3_out, Opcode[9], not_4_out);
  and and_4 (and_4_out, not_2_out, not_3_out);
  and and_5 (and_5_out, not_2_out, Opcode[5]);
  and and_6 (and_6_out, Opcode[9], not_2_out);
  and and_7 (and_7_out, FlagW[1], Opcode[7]);
  and and_8 (RegSrc[1], Opcode[9], not_2_out);
  or or_3 (ALUControl[2], Opcode[6], Opcode[8]);
  and and_9 (ALUControl[1], not_3_out, not_4_out);
  and and_10 (and_10_out, Opcode[7], Opcode[5]);
  and and_11 (and_11_out, not_3_out, not_4_out);
  and and_12 (and_12_out, FlagW[1], not_3_out, Opcode[3]);
  and and_13 (FlagW[0], FlagW[1], Opcode[6]);
  or or_4 (ImmSrc[0], and_3_out, and_4_out);
  or or_5 (RegW, and_5_out, FlagW[1]);
  or or_6 (RegSrc[2], and_6_out, and_7_out);
  or or_7 (ALUControl[0], and_10_out, and_11_out, and_12_out);

  assign ImmSrc[1] = Opcode[8];
  assign PCS = Opcode[8];
  assign RegSrc[0] = Opcode[8];
endmodule

module Control_Unit (
  input  [3:0] ALUFlags,
  input  [15:0] Instr,
  output PCSrc,
  output MemToReg,
  output MemWrite,
  output [2:0] ALUControl,
  output ALUSrc,
  output [1:0] ImmSrc,
  output RegWrite,
  output [2:0] RegSrc
);

  wire Instruction_Decoder1_always, Instruction_Decoder1_memw, Instruction_Decoder1_pcs,
       Instruction_Decoder1_regw;
  wire [1:0] Instruction_Decoder1_flagw;
  wire [3:0] multiplexer_1_out;

  Multiplexer #(.width(4)) multiplexer_1 (
    .in0(Instr[11:8]), .in1(4'b1110), .out(multiplexer_1_out), .sel(Instruction_Decoder1_always));
  Instruction_Decoder Instruction_Decoder1 (
    .Opcode(Instr[15:6]), .\always (Instruction_Decoder1_always), .PCS(Instruction_Decoder1_pcs),
    .MemToReg(MemToReg), .MemW(Instruction_Decoder1_memw), .ALUSrc(ALUSrc), .ImmSrc(ImmSrc),
    .RegW(Instruction_Decoder1_regw), .RegSrc(RegSrc), .ALUControl(ALUControl),
    .FlagW(Instruction_Decoder1_flagw));
  Conditional_Logic Conditional_Logic1 (
    .ALUFlags(ALUFlags), .FlagW(Instruction_Decoder1_flagw), .Cond(multiplexer_1_out),
    .MemW(Instruction_Decoder1_memw), .RegW(Instruction_Decoder1_regw), .PCS(Instruction_Decoder1_pcs),
    .PCSrc(PCSrc), .RegWrite(RegWrite), .MemWrite(MemWrite));

  // Notes on the sheet:
  //   always
  //   1 for writing WriteData to RAM 
  //   ALU operation
  //   1 for using computed Result for PC
  //   1 for using RAM ReadData, else ALUResult
  //   0 for using RD2 1 for ExtImm as ALU SrcB
  //   select which kind of imm exension to ExtImm
  //   1 for RegisterFile write enable (WE3)
  //   select which instruction bits are used for RA2
endmodule

module Adder_1_bit (
  input  CarryIn,
  input  a,
  input  b,
  output CarryOut,
  output Sum
);

  wire and_1_out, and_2_out, and_3_out, and_4_out, and_5_out, and_6_out, and_7_out;

  and and_1 (and_1_out, CarryIn, a);
  and and_2 (and_2_out, CarryIn, b);
  and and_3 (and_3_out, a, b);
  and and_4 (and_4_out, a, ~b, ~CarryIn);  // AND_Gate
  and and_5 (and_5_out, ~a, b, ~CarryIn);  // AND_Gate
  and and_6 (and_6_out, ~a, ~b, CarryIn);  // AND_Gate
  and and_7 (and_7_out, a, b, CarryIn);
  or or_1 (CarryOut, and_1_out, and_2_out, and_3_out);
  or or_2 (Sum, and_4_out, and_5_out, and_6_out, and_7_out);
endmodule

module Adder_32_bit (
  input  CarryIn,
  input  [31:0] A,
  input  [31:0] B,
  output [31:0] Sum,
  output CarryOut
);

  wire adder_1_bit_1_carryout, adder_1_bit_2_carryout, adder_1_bit_3_carryout, adder_1_bit_4_carryout,
       adder_1_bit_5_carryout, adder_1_bit_6_carryout, adder_1_bit_7_carryout, adder_1_bit_8_carryout,
       adder_1_bit_9_carryout, adder_1_bit_10_carryout, adder_1_bit_11_carryout, adder_1_bit_12_carryout,
       adder_1_bit_13_carryout, adder_1_bit_14_carryout, adder_1_bit_15_carryout, adder_1_bit_16_carryout,
       adder_1_bit_17_carryout, adder_1_bit_18_carryout, adder_1_bit_19_carryout, adder_1_bit_20_carryout,
       adder_1_bit_21_carryout, adder_1_bit_22_carryout, adder_1_bit_23_carryout, adder_1_bit_24_carryout,
       adder_1_bit_25_carryout, adder_1_bit_26_carryout, adder_1_bit_27_carryout, adder_1_bit_28_carryout,
       adder_1_bit_29_carryout, adder_1_bit_30_carryout, adder_1_bit_31_carryout;

  Adder_1_bit adder_1_bit_1 (.a(A[0]), .b(B[0]), .CarryIn(CarryIn), .CarryOut(adder_1_bit_1_carryout), .Sum(Sum[0]));
  Adder_1_bit adder_1_bit_2 (
    .a(A[1]), .b(B[1]), .CarryIn(adder_1_bit_1_carryout), .CarryOut(adder_1_bit_2_carryout), .Sum(Sum[1]));
  Adder_1_bit adder_1_bit_3 (
    .a(A[2]), .b(B[2]), .CarryIn(adder_1_bit_2_carryout), .CarryOut(adder_1_bit_3_carryout), .Sum(Sum[2]));
  Adder_1_bit adder_1_bit_4 (
    .a(A[3]), .b(B[3]), .CarryIn(adder_1_bit_3_carryout), .CarryOut(adder_1_bit_4_carryout), .Sum(Sum[3]));
  Adder_1_bit adder_1_bit_5 (
    .a(A[4]), .b(B[4]), .CarryIn(adder_1_bit_4_carryout), .CarryOut(adder_1_bit_5_carryout), .Sum(Sum[4]));
  Adder_1_bit adder_1_bit_6 (
    .a(A[5]), .b(B[5]), .CarryIn(adder_1_bit_5_carryout), .CarryOut(adder_1_bit_6_carryout), .Sum(Sum[5]));
  Adder_1_bit adder_1_bit_7 (
    .a(A[6]), .b(B[6]), .CarryIn(adder_1_bit_6_carryout), .CarryOut(adder_1_bit_7_carryout), .Sum(Sum[6]));
  Adder_1_bit adder_1_bit_8 (
    .a(A[7]), .b(B[7]), .CarryIn(adder_1_bit_7_carryout), .CarryOut(adder_1_bit_8_carryout), .Sum(Sum[7]));
  Adder_1_bit adder_1_bit_9 (
    .a(A[8]), .b(B[8]), .CarryIn(adder_1_bit_8_carryout), .CarryOut(adder_1_bit_9_carryout), .Sum(Sum[8]));
  Adder_1_bit adder_1_bit_10 (
    .a(A[9]), .b(B[9]), .CarryIn(adder_1_bit_9_carryout), .CarryOut(adder_1_bit_10_carryout), .Sum(Sum[9]));
  Adder_1_bit adder_1_bit_11 (
    .a(A[10]), .b(B[10]), .CarryIn(adder_1_bit_10_carryout), .CarryOut(adder_1_bit_11_carryout), .Sum(Sum[10]));
  Adder_1_bit adder_1_bit_12 (
    .a(A[11]), .b(B[11]), .CarryIn(adder_1_bit_11_carryout), .CarryOut(adder_1_bit_12_carryout), .Sum(Sum[11]));
  Adder_1_bit adder_1_bit_13 (
    .a(A[12]), .b(B[12]), .CarryIn(adder_1_bit_12_carryout), .CarryOut(adder_1_bit_13_carryout), .Sum(Sum[12]));
  Adder_1_bit adder_1_bit_14 (
    .a(A[13]), .b(B[13]), .CarryIn(adder_1_bit_13_carryout), .CarryOut(adder_1_bit_14_carryout), .Sum(Sum[13]));
  Adder_1_bit adder_1_bit_15 (
    .a(A[14]), .b(B[14]), .CarryIn(adder_1_bit_14_carryout), .CarryOut(adder_1_bit_15_carryout), .Sum(Sum[14]));
  Adder_1_bit adder_1_bit_16 (
    .a(A[15]), .b(B[15]), .CarryIn(adder_1_bit_15_carryout), .CarryOut(adder_1_bit_16_carryout), .Sum(Sum[15]));
  Adder_1_bit adder_1_bit_17 (
    .a(A[16]), .b(B[16]), .CarryIn(adder_1_bit_16_carryout), .CarryOut(adder_1_bit_17_carryout), .Sum(Sum[16]));
  Adder_1_bit adder_1_bit_18 (
    .a(A[17]), .b(B[17]), .CarryIn(adder_1_bit_17_carryout), .CarryOut(adder_1_bit_18_carryout), .Sum(Sum[17]));
  Adder_1_bit adder_1_bit_19 (
    .a(A[18]), .b(B[18]), .CarryIn(adder_1_bit_18_carryout), .CarryOut(adder_1_bit_19_carryout), .Sum(Sum[18]));
  Adder_1_bit adder_1_bit_20 (
    .a(A[19]), .b(B[19]), .CarryIn(adder_1_bit_19_carryout), .CarryOut(adder_1_bit_20_carryout), .Sum(Sum[19]));
  Adder_1_bit adder_1_bit_21 (
    .a(A[20]), .b(B[20]), .CarryIn(adder_1_bit_20_carryout), .CarryOut(adder_1_bit_21_carryout), .Sum(Sum[20]));
  Adder_1_bit adder_1_bit_22 (
    .a(A[21]), .b(B[21]), .CarryIn(adder_1_bit_21_carryout), .CarryOut(adder_1_bit_22_carryout), .Sum(Sum[21]));
  Adder_1_bit adder_1_bit_23 (
    .a(A[22]), .b(B[22]), .CarryIn(adder_1_bit_22_carryout), .CarryOut(adder_1_bit_23_carryout), .Sum(Sum[22]));
  Adder_1_bit adder_1_bit_24 (
    .a(A[23]), .b(B[23]), .CarryIn(adder_1_bit_23_carryout), .CarryOut(adder_1_bit_24_carryout), .Sum(Sum[23]));
  Adder_1_bit adder_1_bit_25 (
    .a(A[24]), .b(B[24]), .CarryIn(adder_1_bit_24_carryout), .CarryOut(adder_1_bit_25_carryout), .Sum(Sum[24]));
  Adder_1_bit adder_1_bit_26 (
    .a(A[25]), .b(B[25]), .CarryIn(adder_1_bit_25_carryout), .CarryOut(adder_1_bit_26_carryout), .Sum(Sum[25]));
  Adder_1_bit adder_1_bit_27 (
    .a(A[26]), .b(B[26]), .CarryIn(adder_1_bit_26_carryout), .CarryOut(adder_1_bit_27_carryout), .Sum(Sum[26]));
  Adder_1_bit adder_1_bit_28 (
    .a(A[27]), .b(B[27]), .CarryIn(adder_1_bit_27_carryout), .CarryOut(adder_1_bit_28_carryout), .Sum(Sum[27]));
  Adder_1_bit adder_1_bit_29 (
    .a(A[28]), .b(B[28]), .CarryIn(adder_1_bit_28_carryout), .CarryOut(adder_1_bit_29_carryout), .Sum(Sum[28]));
  Adder_1_bit adder_1_bit_30 (
    .a(A[29]), .b(B[29]), .CarryIn(adder_1_bit_29_carryout), .CarryOut(adder_1_bit_30_carryout), .Sum(Sum[29]));
  Adder_1_bit adder_1_bit_31 (
    .a(A[30]), .b(B[30]), .CarryIn(adder_1_bit_30_carryout), .CarryOut(adder_1_bit_31_carryout), .Sum(Sum[30]));
  Adder_1_bit adder_1_bit_32 (
    .a(A[31]), .b(B[31]), .CarryIn(adder_1_bit_31_carryout), .CarryOut(CarryOut), .Sum(Sum[31]));

  // Other names for the same wires on the sheet: A0[7:0] = A[7:0]; A1[7:0] = A[15:8]; A2[7:0] = A[23:16];
  //   A3[7:0] = A[31:24]; B0[7:0] = B[7:0]; B1[7:0] = B[15:8]; B2[7:0] = B[23:16]; B3[7:0] = B[31:24];
  //   S0[7:0] = Sum[7:0]; S1[7:0] = Sum[15:8]; S2[7:0] = Sum[23:16]; S3[7:0] = Sum[31:24]
endmodule

module Zero_Detect_32_bit (
  input  [31:0] A,
  output B
);

  nor nor_1 (B, A[0], A[1], A[2], A[3], A[4], A[5], A[6], A[7], A[8], A[9], A[10], A[11], A[12], A[13], A[14], A[15], A[16], A[17], A[18], A[19], A[20], A[21], A[22], A[23], A[24], A[25], A[26], A[27], A[28], A[29], A[30], A[31]);
endmodule

module RegisterSelect (
  input  [2:0] RegSel,
  input  [15:0] instr,
  output [3:0] RA1,
  output [3:0] RA2,
  output [3:0] RA3
);

  wire [2:0] multiplexer_1_out, multiplexer_2_out, multiplexer_3_out;

  Multiplexer #(.width(3)) multiplexer_1 (
    .in0(instr[5:3]), .in1(instr[10:8]), .out(multiplexer_1_out), .sel(RegSel[1]));
  Multiplexer #(.width(3)) multiplexer_2 (
    .in0(instr[8:6]), .in1(instr[10:8]), .out(multiplexer_2_out), .sel(RegSel[2]));
  assign RA1 = {{1{1'b0}}, multiplexer_3_out};  // Bit_Extender bit_extender_1
  Multiplexer #(.width(3)) multiplexer_3 (.in0(instr[2:0]), .in1(instr[5:3]), .out(multiplexer_3_out), .sel(RegSel[0]));
  assign RA2 = {{1{1'b0}}, multiplexer_1_out};  // Bit_Extender bit_extender_2
  assign RA3 = {{1{1'b0}}, multiplexer_2_out};  // Bit_Extender bit_extender_3

  // Notes on the sheet:
  //   Rm
  //   Rn
  //   Rd
endmodule

module main_1 (
);

  wire clk_out, clock_1_out, clock_2_out, control_unit_1_alusrc, control_unit_1_memtoreg,
       control_unit_1_memwrite, control_unit_1_pcsrc, control_unit_1_regwrite, por_1_out;
  wire [1:0] control_unit_1_immsrc, control_unit_1_regsrc;
  wire [2:0] control_unit_1_alucontrol, multiplexer_2_out, multiplexer_3_out, multiplexer_4_out;
  wire [2:2] control_unit_1_regsrc_2;
  wire [3:0] alu_1_aluflags;
  wire [15:0] ROM1_data;
  wire [31:0] adder_1_out, adder_2_out, alu_1_result, immediate_1_imm32, multiplexer_1_out,
       multiplexer_5_out, multiplexer_6_out, PC_q, RAM1_dout, registerfile_1_rd1, registerfile_1_rd2;

  Clock clk (.out(clk_out));
  LED led_1 (.in(clk_out));
  Register #(.width(32)) PC (.D(multiplexer_1_out), .en(1'b1), .clk(clock_1_out), .Q(PC_q), .clr(por_1_out));
  Multiplexer #(.width(32)) multiplexer_1 (
    .in0(adder_1_out), .in1(multiplexer_6_out), .out(multiplexer_1_out), .sel(control_unit_1_pcsrc));
  Clock clock_1 (.out(clock_1_out));
  POR #(.PorHighDuration(1), .porsize(1)) por_1 (.out(por_1_out));
  ROM #(.addrWidth(16), .dataWidth(16)) ROM1 (.addr(PC_q[16:1]), .data(ROM1_data));
  Adder #(.width(32)) adder_1 (.a(PC_q), .b(32'h2), .out(adder_1_out));  // open: cin, cout
  // Probe on control_unit_1_pcsrc
  // Probe on adder_1_out
  // Probe on ROM1_data
  // Probe on control_unit_1_regsrc_2[2]
  // Probe on multiplexer_2_out
  Multiplexer #(.width(3)) multiplexer_2 (
    .in0(ROM1_data[5:3]), .in1(ROM1_data[10:8]), .out(multiplexer_2_out), .sel(control_unit_1_regsrc_2[2]));
  // Probe on multiplexer_3_out
  Multiplexer #(.width(3)) multiplexer_3 (
    .in0(ROM1_data[8:6]), .in1(ROM1_data[10:8]), .out(multiplexer_3_out), .sel(control_unit_1_regsrc_2[2]));
  // Probe on multiplexer_4_out
  Multiplexer #(.width(3)) multiplexer_4 (
    .in0(ROM1_data[2:0]), .in1(ROM1_data[10:8]), .out(multiplexer_4_out), .sel(control_unit_1_regsrc_2[2]));
  Adder #(.width(32)) adder_2 (.a(adder_1_out), .b(32'h2), .out(adder_2_out));  // open: cin, cout
  Control_Unit control_unit_1 (
    .Instr(ROM1_data), .ALUFlags(alu_1_aluflags), .MemToReg(control_unit_1_memtoreg),
    .MemWrite(control_unit_1_memwrite), .ALUControl(control_unit_1_alucontrol),
    .ALUSrc(control_unit_1_alusrc), .ImmSrc(control_unit_1_immsrc), .RegWrite(control_unit_1_regwrite),
    .RegSrc({control_unit_1_regsrc_2[2], control_unit_1_regsrc}), .PCSrc(control_unit_1_pcsrc));
  // Probe on adder_2_out
  // Probe on control_unit_1_immsrc
  // Probe on control_unit_1_regsrc
  RegisterFile registerfile_1 (
    .WE3(control_unit_1_regwrite), .SP_PC(control_unit_1_regsrc), .A2(multiplexer_3_out),
    .A3(multiplexer_4_out), .A1(multiplexer_2_out), .R15(adder_2_out), .WD3(multiplexer_6_out),
    .RD1(registerfile_1_rd1), .RD2(registerfile_1_rd2));
  Immediate immediate_1 (.ImmSrc(control_unit_1_immsrc), .Instr(ROM1_data), .Imm32(immediate_1_imm32));
  // Probe on control_unit_1_alusrc
  Multiplexer #(.width(32)) multiplexer_5 (
    .in0(registerfile_1_rd2), .in1(immediate_1_imm32), .out(multiplexer_5_out), .sel(control_unit_1_alusrc));
  // Probe on immediate_1_imm32
  // Probe on multiplexer_6_out
  // Probe on control_unit_1_alucontrol
  // Probe on registerfile_1_rd1
  // Probe on multiplexer_5_out
  // Probe on registerfile_1_rd2
  ALU alu_1 (
    .A(registerfile_1_rd1), .B(multiplexer_5_out), .ALUControl(control_unit_1_alucontrol),
    .Result(alu_1_result), .ALUFlags(alu_1_aluflags));
  // Probe on control_unit_1_memwrite
  RAM #(.addrWidth(16), .asyncread("true"), .dataWidth(32)) RAM1 (
    .addr(alu_1_result[17:2]), .we(control_unit_1_memwrite), .clk(clock_2_out), .din(registerfile_1_rd2),
    .dout(RAM1_dout));  // open: oe
  Clock clock_2 (.out(clock_2_out));
  // Probe on control_unit_1_memtoreg
  // Probe on RAM1_dout
  Multiplexer #(.width(32)) multiplexer_6 (
    .in0(alu_1_result), .in1(RAM1_dout), .out(multiplexer_6_out), .sel(control_unit_1_memtoreg));

  // Notes on the sheet:
  //   contents of ROM1 (hex, n*v repeats v):
  //   2000 9000 2001 9001 9800 9901 1842 d402 9100 9201 e7f8 e7fe
endmodule

module main_2 (
);

  wire clk_out, clock_1_out, clock_2_out, control_unit_1_alusrc, control_unit_1_memwrite,
       control_unit_1_pcsrc, control_unit_1_regwrite, por_1_out;
  wire [1:0] control_unit_1_immsrc, control_unit_1_regsrc;
  wire [2:0] control_unit_1_alucontrol, multiplexer_2_out, multiplexer_3_out, multiplexer_4_out;
  wire [2:2] control_unit_1_regsrc_2;
  wire [3:0] alu_1_aluflags;
  wire [15:0] alu_1_result_2, ROM1_data;
  wire [31:0] adder_1_out, adder_2_out, alu_1_result, immediate_1_imm32, multiplexer_1_out,
       multiplexer_5_out, PC_q, registerfile_1_rd1, registerfile_1_rd2;

  Clock clk (.out(clk_out));
  LED led_1 (.in(clk_out));
  Register #(.width(32)) PC (.D(multiplexer_1_out), .en(1'b1), .clk(clock_1_out), .Q(PC_q), .clr(por_1_out));
  Multiplexer #(.width(32)) multiplexer_1 (
    .in0(adder_1_out), .in1({alu_1_result[31:18], alu_1_result_2, alu_1_result[1:0]}),
    .out(multiplexer_1_out), .sel(control_unit_1_pcsrc));
  Clock clock_1 (.out(clock_1_out));
  POR #(.PorHighDuration(1), .porsize(1)) por_1 (.out(por_1_out));
  ROM #(.addrWidth(16), .dataWidth(16)) ROM1 (.addr(PC_q[16:1]), .data(ROM1_data));
  Adder #(.width(32)) adder_1 (.a(PC_q), .b(32'h2), .out(adder_1_out));  // open: cin, cout
  // Probe on control_unit_1_pcsrc
  // Probe on adder_1_out
  // Probe on ROM1_data
  // Probe on multiplexer_2_out
  Multiplexer #(.width(3)) multiplexer_2 (
    .in0(ROM1_data[5:3]), .in1(ROM1_data[10:8]), .out(multiplexer_2_out), .sel(control_unit_1_regsrc_2[2]));
  // Probe on multiplexer_3_out
  Multiplexer #(.width(3)) multiplexer_3 (
    .in0(ROM1_data[8:6]), .in1(ROM1_data[10:8]), .out(multiplexer_3_out), .sel(control_unit_1_regsrc_2[2]));
  // Probe on multiplexer_4_out
  Multiplexer #(.width(3)) multiplexer_4 (
    .in0(ROM1_data[2:0]), .in1(ROM1_data[10:8]), .out(multiplexer_4_out), .sel(control_unit_1_regsrc_2[2]));
  Adder #(.width(32)) adder_2 (.a(adder_1_out), .b(32'h2), .out(adder_2_out));  // open: cin, cout
  Control_Unit control_unit_1 (
    .Instr(ROM1_data), .ALUFlags(alu_1_aluflags), .MemWrite(control_unit_1_memwrite),
    .ALUControl(control_unit_1_alucontrol), .ALUSrc(control_unit_1_alusrc), .ImmSrc(control_unit_1_immsrc),
    .RegWrite(control_unit_1_regwrite), .RegSrc({control_unit_1_regsrc_2[2], control_unit_1_regsrc}),
    .PCSrc(control_unit_1_pcsrc));  // open: MemToReg
  // Probe on adder_2_out
  RegisterFile registerfile_1 (
    .WE3(control_unit_1_regwrite), .SP_PC(control_unit_1_regsrc), .A2(multiplexer_3_out),
    .A3(multiplexer_4_out), .A1(multiplexer_2_out), .R15(adder_2_out),
    .WD3({alu_1_result[31:18], alu_1_result_2, alu_1_result[1:0]}), .RD1(registerfile_1_rd1),
    .RD2(registerfile_1_rd2));
  Immediate immediate_1 (.ImmSrc(control_unit_1_immsrc), .Instr(ROM1_data), .Imm32(immediate_1_imm32));
  Multiplexer #(.width(32)) multiplexer_5 (
    .in0(registerfile_1_rd2), .in1(immediate_1_imm32), .out(multiplexer_5_out), .sel(control_unit_1_alusrc));
  // Probe on immediate_1_imm32
  // Probe on {alu_1_result[31:18], alu_1_result_2, alu_1_result[1:0]}
  // Probe on control_unit_1_alucontrol
  // Probe on registerfile_1_rd1
  // Probe on multiplexer_5_out
  // Probe on registerfile_1_rd2
  ALU alu_1 (
    .A(registerfile_1_rd1), .B(multiplexer_5_out), .ALUControl(control_unit_1_alucontrol),
    .Result({alu_1_result[31:18], alu_1_result_2, alu_1_result[1:0]}), .ALUFlags(alu_1_aluflags));
  // Probe on control_unit_1_memwrite
  RAM #(.addrWidth(16), .asyncread("true"), .dataWidth(32)) RAM1 (
    .addr(alu_1_result_2), .we(control_unit_1_memwrite), .clk(clock_2_out), .din(registerfile_1_rd2));  // open: oe, dout
  Clock clock_2 (.out(clock_2_out));

  // Notes on the sheet:
  //   contents of ROM1 (hex, n*v repeats v):
  //   200a 9001
endmodule

module main_3 (
  output [31:0] ALUResult
);

  wire clock_1_out, control_unit_1_alusrc, control_unit_1_pcsrc, control_unit_1_regwrite, por_1_out;
  wire [1:0] control_unit_1_immsrc, control_unit_1_regsrc;
  wire [2:0] control_unit_1_alucontrol, multiplexer_2_out, multiplexer_3_out, multiplexer_4_out;
  wire [2:2] control_unit_1_regsrc_2;
  wire [3:0] alu_1_aluflags;
  wire [15:0] ROM1_data;
  wire [31:0] adder_1_out, adder_2_out, immediate_1_imm32, multiplexer_1_out, multiplexer_5_out, PC_q,
       registerfile_1_rd1, registerfile_1_rd2;

  Register #(.width(32)) PC (.D(multiplexer_1_out), .en(1'b1), .clk(clock_1_out), .Q(PC_q), .clr(por_1_out));
  Multiplexer #(.width(32)) multiplexer_1 (
    .in0(adder_1_out), .in1(ALUResult), .out(multiplexer_1_out), .sel(control_unit_1_pcsrc));
  Clock clock_1 (.out(clock_1_out));
  POR #(.PorHighDuration(1), .porsize(1)) por_1 (.out(por_1_out));
  ROM #(.addrWidth(16), .dataWidth(16)) ROM1 (.addr(PC_q[16:1]), .data(ROM1_data));
  Adder #(.width(32)) adder_1 (.a(PC_q), .b(32'h2), .out(adder_1_out));  // open: cin, cout
  // Probe on control_unit_1_pcsrc
  // Probe on adder_1_out
  // Probe on ROM1_data
  // Probe on control_unit_1_regsrc_2[2]
  // Probe on multiplexer_2_out
  Multiplexer #(.width(3)) multiplexer_2 (
    .in0(ROM1_data[5:3]), .in1(ROM1_data[10:8]), .out(multiplexer_2_out), .sel(control_unit_1_regsrc_2[2]));
  // Probe on multiplexer_3_out
  Multiplexer #(.width(3)) multiplexer_3 (
    .in0(ROM1_data[8:6]), .in1(ROM1_data[10:8]), .out(multiplexer_3_out), .sel(control_unit_1_regsrc_2[2]));
  // Probe on multiplexer_4_out
  Multiplexer #(.width(3)) multiplexer_4 (
    .in0(ROM1_data[2:0]), .in1(ROM1_data[10:8]), .out(multiplexer_4_out), .sel(control_unit_1_regsrc_2[2]));
  Adder #(.width(32)) adder_2 (.a(adder_1_out), .b(32'h2), .out(adder_2_out));  // open: cin, cout
  Control_Unit control_unit_1 (
    .Instr(ROM1_data), .ALUFlags(alu_1_aluflags), .ALUControl(control_unit_1_alucontrol),
    .ALUSrc(control_unit_1_alusrc), .ImmSrc(control_unit_1_immsrc), .RegWrite(control_unit_1_regwrite),
    .RegSrc({control_unit_1_regsrc_2[2], control_unit_1_regsrc}), .PCSrc(control_unit_1_pcsrc));  // open: MemToReg, MemWrite
  // Probe on adder_2_out
  // Probe on control_unit_1_immsrc
  // Probe on control_unit_1_regsrc
  RegisterFile registerfile_1 (
    .WE3(control_unit_1_regwrite), .SP_PC(control_unit_1_regsrc), .A2(multiplexer_3_out),
    .A3(multiplexer_4_out), .A1(multiplexer_2_out), .R15(adder_2_out), .WD3(ALUResult),
    .RD1(registerfile_1_rd1), .RD2(registerfile_1_rd2));
  Immediate immediate_1 (.ImmSrc(control_unit_1_immsrc), .Instr(ROM1_data), .Imm32(immediate_1_imm32));
  Multiplexer #(.width(32)) multiplexer_5 (
    .in0(registerfile_1_rd2), .in1(immediate_1_imm32), .out(multiplexer_5_out), .sel(control_unit_1_alusrc));
  // Probe on immediate_1_imm32
  // Probe on ALUResult
  // Probe on control_unit_1_alucontrol
  // Probe on registerfile_1_rd1
  // Probe on multiplexer_5_out
  // Probe on alu_1_aluflags
  ALU alu_1 (
    .A(registerfile_1_rd1), .B(multiplexer_5_out), .ALUControl(control_unit_1_alucontrol),
    .Result(ALUResult), .ALUFlags(alu_1_aluflags));

  // Notes on the sheet:
  //   contents of ROM1 (hex, n*v repeats v):
  //   200a 3801 d1fd e7fe
  //   NZCV
endmodule

module main_4 (
  output [3:0] ALUFlags,
  output [31:0] ALUResult
);

  wire clock_1_out, control_unit_1_alusrc, control_unit_1_pcsrc, control_unit_1_regwrite, por_1_out;
  wire [1:0] control_unit_1_immsrc, control_unit_1_regsrc;
  wire [2:0] control_unit_1_alucontrol, multiplexer_2_out, multiplexer_3_out, multiplexer_4_out;
  wire [2:2] control_unit_1_regsrc_2;
  wire [15:0] ROM1_data;
  wire [31:0] adder_1_out, adder_2_out, immediate_1_imm32, multiplexer_1_out, multiplexer_5_out, PC_q,
       registerfile_1_rd1, registerfile_1_rd2;

  Register #(.width(32)) PC (.D(multiplexer_1_out), .en(1'b1), .clk(clock_1_out), .Q(PC_q), .clr(por_1_out));
  Multiplexer #(.width(32)) multiplexer_1 (
    .in0(adder_1_out), .in1(ALUResult), .out(multiplexer_1_out), .sel(control_unit_1_pcsrc));
  Clock clock_1 (.out(clock_1_out));
  POR #(.PorHighDuration(1), .porsize(1)) por_1 (.out(por_1_out));
  ROM #(.addrWidth(16), .dataWidth(16)) ROM1 (.addr(PC_q[16:1]), .data(ROM1_data));
  Adder #(.width(32)) adder_1 (.a(PC_q), .b(32'h2), .out(adder_1_out));  // open: cin, cout
  // Probe on control_unit_1_pcsrc
  // Probe on adder_1_out
  // Probe on ROM1_data
  // Probe on multiplexer_2_out
  Multiplexer #(.width(3)) multiplexer_2 (
    .in0(ROM1_data[5:3]), .in1(ROM1_data[10:8]), .out(multiplexer_2_out), .sel(control_unit_1_regsrc_2[2]));
  // Probe on multiplexer_3_out
  Multiplexer #(.width(3)) multiplexer_3 (
    .in0(ROM1_data[8:6]), .in1(ROM1_data[10:8]), .out(multiplexer_3_out), .sel(control_unit_1_regsrc_2[2]));
  // Probe on multiplexer_4_out
  Multiplexer #(.width(3)) multiplexer_4 (
    .in0(ROM1_data[2:0]), .in1(ROM1_data[10:8]), .out(multiplexer_4_out), .sel(control_unit_1_regsrc_2[2]));
  Adder #(.width(32)) adder_2 (.a(adder_1_out), .b(32'h2), .out(adder_2_out));  // open: cin, cout
  Control_Unit control_unit_1 (
    .Instr(ROM1_data), .ALUControl(control_unit_1_alucontrol), .ALUSrc(control_unit_1_alusrc),
    .ImmSrc(control_unit_1_immsrc), .RegWrite(control_unit_1_regwrite),
    .RegSrc({control_unit_1_regsrc_2[2], control_unit_1_regsrc}), .PCSrc(control_unit_1_pcsrc));  // open: ALUFlags, MemToReg, MemWrite
  // Probe on adder_2_out
  RegisterFile registerfile_1 (
    .WE3(control_unit_1_regwrite), .SP_PC(control_unit_1_regsrc), .A2(multiplexer_3_out),
    .A3(multiplexer_4_out), .A1(multiplexer_2_out), .R15(adder_2_out), .WD3(ALUResult),
    .RD1(registerfile_1_rd1), .RD2(registerfile_1_rd2));
  Immediate immediate_1 (.ImmSrc(control_unit_1_immsrc), .Instr(ROM1_data), .Imm32(immediate_1_imm32));
  Multiplexer #(.width(32)) multiplexer_5 (
    .in0(registerfile_1_rd2), .in1(immediate_1_imm32), .out(multiplexer_5_out), .sel(control_unit_1_alusrc));
  // Probe on immediate_1_imm32
  // Probe on ALUResult
  // Probe on control_unit_1_alucontrol
  // Probe on registerfile_1_rd1
  // Probe on multiplexer_5_out
  ALU alu_1 (
    .A(registerfile_1_rd1), .B(multiplexer_5_out), .ALUControl(control_unit_1_alucontrol),
    .Result(ALUResult), .ALUFlags(ALUFlags));

  // Notes on the sheet:
  //   contents of ROM1 (hex, n*v repeats v):
  //   2000 3001 e7fd
endmodule

module main_5 (
  output [3:0] ALUFlags,
  output [31:0] ALUResult
);

  wire clock_1_out, control_unit_1_alusrc, control_unit_1_regwrite, por_1_out;
  wire [1:0] control_unit_1_immsrc, control_unit_1_regsrc;
  wire [2:0] control_unit_1_alucontrol, multiplexer_1_out, multiplexer_2_out, multiplexer_3_out;
  wire [2:2] control_unit_1_regsrc_2;
  wire [15:0] ROM1_data;
  wire [31:0] adder_1_out, immediate_1_imm32, multiplexer_4_out, PC_q, registerfile_1_rd1, registerfile_1_rd2;

  Register #(.width(32)) PC (.D(adder_1_out), .en(1'b1), .clk(clock_1_out), .Q(PC_q), .clr(por_1_out));
  Clock clock_1 (.out(clock_1_out));
  POR #(.PorHighDuration(1), .porsize(1)) por_1 (.out(por_1_out));
  ROM #(.addrWidth(16), .dataWidth(16)) ROM1 (.addr(PC_q[16:1]), .data(ROM1_data));
  Adder #(.width(32)) adder_1 (.a(PC_q), .b(32'h2), .out(adder_1_out));  // open: cin, cout
  // Probe on multiplexer_1_out
  Multiplexer #(.width(3)) multiplexer_1 (
    .in0(ROM1_data[5:3]), .in1(ROM1_data[10:8]), .out(multiplexer_1_out), .sel(control_unit_1_regsrc_2[2]));
  // Probe on multiplexer_2_out
  Multiplexer #(.width(3)) multiplexer_2 (
    .in0(ROM1_data[8:6]), .in1(ROM1_data[10:8]), .out(multiplexer_2_out), .sel(control_unit_1_regsrc_2[2]));
  // Probe on multiplexer_3_out
  Multiplexer #(.width(3)) multiplexer_3 (
    .in0(ROM1_data[2:0]), .in1(ROM1_data[10:8]), .out(multiplexer_3_out), .sel(control_unit_1_regsrc_2[2]));
  Control_Unit control_unit_1 (
    .Instr(ROM1_data), .ALUControl(control_unit_1_alucontrol), .ALUSrc(control_unit_1_alusrc),
    .ImmSrc(control_unit_1_immsrc), .RegWrite(control_unit_1_regwrite),
    .RegSrc({control_unit_1_regsrc_2[2], control_unit_1_regsrc}));  // open: ALUFlags, MemToReg, MemWrite, PCSrc
  RegisterFile registerfile_1 (
    .WE3(control_unit_1_regwrite), .SP_PC(control_unit_1_regsrc), .A2(multiplexer_2_out),
    .A3(multiplexer_3_out), .A1(multiplexer_1_out), .WD3(ALUResult), .RD1(registerfile_1_rd1),
    .RD2(registerfile_1_rd2));  // open: R15
  Immediate immediate_1 (.ImmSrc(control_unit_1_immsrc), .Instr(ROM1_data), .Imm32(immediate_1_imm32));
  Multiplexer #(.width(32)) multiplexer_4 (
    .in0(registerfile_1_rd2), .in1(immediate_1_imm32), .out(multiplexer_4_out), .sel(control_unit_1_alusrc));
  // Probe on immediate_1_imm32
  // Probe on ALUResult
  // Probe on control_unit_1_alucontrol
  // Probe on registerfile_1_rd1
  // Probe on multiplexer_4_out
  ALU alu_1 (
    .A(registerfile_1_rd1), .B(multiplexer_4_out), .ALUControl(control_unit_1_alucontrol),
    .Result(ALUResult), .ALUFlags(ALUFlags));

  // Notes on the sheet:
  //   contents of ROM1 (hex, n*v repeats v):
  //   2534 2316 18ec
endmodule

module main_6 (
  input  [15:0] Instruction,
  output [3:0] ALUFlags,
  output [31:0] ALUResult
);

  wire control_unit_1_alusrc, control_unit_1_regwrite;
  wire [1:0] control_unit_1_immsrc, control_unit_1_regsrc;
  wire [2:0] control_unit_1_alucontrol, multiplexer_1_out, multiplexer_2_out, multiplexer_3_out;
  wire [2:2] control_unit_1_regsrc_2;
  wire [31:0] immediate_1_imm32, multiplexer_4_out, registerfile_1_rd1, registerfile_1_rd2;

  // Probe on multiplexer_1_out
  Multiplexer #(.width(3)) multiplexer_1 (
    .in0(Instruction[5:3]), .in1(Instruction[10:8]), .out(multiplexer_1_out), .sel(control_unit_1_regsrc_2[2]));
  // Probe on multiplexer_2_out
  Multiplexer #(.width(3)) multiplexer_2 (
    .in0(Instruction[8:6]), .in1(Instruction[10:8]), .out(multiplexer_2_out), .sel(control_unit_1_regsrc_2[2]));
  // Probe on multiplexer_3_out
  Multiplexer #(.width(3)) multiplexer_3 (
    .in0(Instruction[2:0]), .in1(Instruction[10:8]), .out(multiplexer_3_out), .sel(control_unit_1_regsrc_2[2]));
  Control_Unit control_unit_1 (
    .Instr(Instruction), .ALUControl(control_unit_1_alucontrol), .ALUSrc(control_unit_1_alusrc),
    .ImmSrc(control_unit_1_immsrc), .RegWrite(control_unit_1_regwrite),
    .RegSrc({control_unit_1_regsrc_2[2], control_unit_1_regsrc}));  // open: ALUFlags, MemToReg, MemWrite, PCSrc
  RegisterFile registerfile_1 (
    .WE3(control_unit_1_regwrite), .SP_PC(control_unit_1_regsrc), .A2(multiplexer_2_out),
    .A3(multiplexer_3_out), .A1(multiplexer_1_out), .WD3(ALUResult), .RD1(registerfile_1_rd1),
    .RD2(registerfile_1_rd2));  // open: R15
  Immediate immediate_1 (.ImmSrc(control_unit_1_immsrc), .Instr(Instruction), .Imm32(immediate_1_imm32));
  Multiplexer #(.width(32)) multiplexer_4 (
    .in0(registerfile_1_rd2), .in1(immediate_1_imm32), .out(multiplexer_4_out), .sel(control_unit_1_alusrc));
  // Probe on immediate_1_imm32
  // Probe on ALUResult
  // Probe on control_unit_1_alucontrol
  // Probe on registerfile_1_rd1
  // Probe on multiplexer_4_out
  ALU alu_1 (
    .A(registerfile_1_rd1), .B(multiplexer_4_out), .ALUControl(control_unit_1_alucontrol),
    .Result(ALUResult), .ALUFlags(ALUFlags));
endmodule

module main_7 (
  input  [15:0] Instruction,
  output [3:0] ALUFlags,
  output [31:0] ALUResult
);

  wire control_unit_1_regwrite;
  wire [1:0] control_unit_1_regsrc;
  wire [2:0] control_unit_1_alucontrol, multiplexer_1_out, multiplexer_2_out, multiplexer_3_out;
  wire [2:2] control_unit_1_regsrc_2;
  wire [31:0] registerfile_1_rd1, registerfile_1_rd2;

  // Probe on multiplexer_1_out
  Multiplexer #(.width(3)) multiplexer_1 (
    .in0(Instruction[5:3]), .in1(Instruction[10:8]), .out(multiplexer_1_out), .sel(control_unit_1_regsrc_2[2]));
  // Probe on multiplexer_2_out
  Multiplexer #(.width(3)) multiplexer_2 (
    .in0(Instruction[8:6]), .in1(Instruction[10:8]), .out(multiplexer_2_out), .sel(control_unit_1_regsrc_2[2]));
  // Probe on multiplexer_3_out
  Multiplexer #(.width(3)) multiplexer_3 (
    .in0(Instruction[2:0]), .in1(Instruction[10:8]), .out(multiplexer_3_out), .sel(control_unit_1_regsrc_2[2]));
  Control_Unit control_unit_1 (
    .Instr(Instruction), .ALUControl(control_unit_1_alucontrol), .RegWrite(control_unit_1_regwrite),
    .RegSrc({control_unit_1_regsrc_2[2], control_unit_1_regsrc}));  // open: ALUFlags, MemToReg, MemWrite, ALUSrc, ImmSrc, PCSrc
  RegisterFile registerfile_1 (
    .WE3(control_unit_1_regwrite), .SP_PC(control_unit_1_regsrc), .A2(multiplexer_2_out),
    .A3(multiplexer_3_out), .A1(multiplexer_1_out), .WD3(ALUResult), .RD1(registerfile_1_rd1),
    .RD2(registerfile_1_rd2));  // open: R15
  // Probe on registerfile_1_rd1
  // Probe on registerfile_1_rd2
  // Probe on ALUResult
  // Probe on control_unit_1_alucontrol
  ALU alu_1 (
    .A(registerfile_1_rd1), .B(registerfile_1_rd2), .ALUControl(control_unit_1_alucontrol),
    .Result(ALUResult), .ALUFlags(ALUFlags));
endmodule

module main_8 (
  input  [2:0] ALUControl,
  input  [2:0] RA1,
  input  [2:0] RA2,
  input  [2:0] RA3,
  input  RegWrite,
  output [3:0] ALUFlags,
  output [31:0] ALUResult
);

  wire [31:0] registerfile_1_rd1, registerfile_1_rd2;

  RegisterFile registerfile_1 (
    .WE3(RegWrite), .A2(RA2), .A3(RA3), .A1(RA1), .WD3(ALUResult), .RD1(registerfile_1_rd1),
    .RD2(registerfile_1_rd2));  // open: SP_PC, R15
  // Probe on registerfile_1_rd1
  // Probe on registerfile_1_rd2
  // Probe on ALUResult
  ALU alu_1 (
    .A(registerfile_1_rd1), .B(registerfile_1_rd2), .ALUControl(ALUControl), .Result(ALUResult),
    .ALUFlags(ALUFlags));
endmodule

module main_9 (
  input  [2:0] ALUControl,
  input  [31:0] SrcB,
  output [3:0] ALUFlags,
  output [31:0] ALUResult
);

  wire clock_1_out;
  wire [31:0] Accumulator_q;

  Register #(.width(32)) Accumulator (.D(ALUResult), .clk(clock_1_out), .Q(Accumulator_q));  // open: en, clr
  Clock clock_1 (.out(clock_1_out));
  ALU alu_1 (.A(Accumulator_q), .B(SrcB), .ALUControl(ALUControl), .Result(ALUResult), .ALUFlags(ALUFlags));
endmodule

module main_10 (
  input  [2:0] ALUControl,
  input  [31:0] SrcA,
  input  [31:0] SrcB,
  output [3:0] ALUFlags,
  output [31:0] ALUResult
);

  ALU alu_1 (.A(SrcA), .B(SrcB), .ALUControl(ALUControl), .Result(ALUResult), .ALUFlags(ALUFlags));
endmodule

module main_0 (
);

  wire clk_out, clock_1_out, clock_2_out, Control_Unit1_alusrc, Control_Unit1_memtoreg,
       Control_Unit1_memwrite, Control_Unit1_pcsrc, Control_Unit1_regwrite, por_1_out;
  wire [1:0] Control_Unit1_immsrc, Control_Unit1_regsrc;
  wire [2:0] Control_Unit1_alucontrol, multiplexer_2_out, multiplexer_3_out, multiplexer_4_out;
  wire [2:2] Control_Unit1_regsrc_2;
  wire [3:0] ALU1_aluflags;
  wire [15:0] ROM1_data;
  wire [31:0] adder_1_out, adder_2_out, ALU1_result, Immediate1_imm32, multiplexer_1_out, multiplexer_5_out,
       PC_q, RAM1_dout, RegisterFile1_p6, RegisterFile1_p8, RegisterFile1_p9;

  Clock clk (.out(clk_out));
  LED led_1 (.in(clk_out));
  Register #(.width(32)) PC (.D(multiplexer_1_out), .en(1'b1), .clk(clock_1_out), .Q(PC_q), .clr(por_1_out));
  Multiplexer #(.width(32)) multiplexer_1 (
    .in0(adder_1_out), .in1(RegisterFile1_p6), .out(multiplexer_1_out), .sel(Control_Unit1_pcsrc));
  Clock clock_1 (.out(clock_1_out));
  POR #(.PorHighDuration(1), .porsize(1)) por_1 (.out(por_1_out));
  ROM #(.addrWidth(16), .dataWidth(16)) ROM1 (.addr(PC_q[16:1]), .data(ROM1_data));
  Adder #(.width(32)) adder_1 (.a(PC_q), .b(32'h2), .out(adder_1_out));  // open: cin, cout
  // Probe on Control_Unit1_pcsrc
  // Probe on adder_1_out
  // Probe on ROM1_data
  // Probe on Control_Unit1_regsrc_2[2]
  // Probe on multiplexer_2_out
  Multiplexer #(.width(3)) multiplexer_2 (
    .in0(ROM1_data[5:3]), .in1(ROM1_data[10:8]), .out(multiplexer_2_out), .sel(Control_Unit1_regsrc_2[2]));
  // Probe on multiplexer_3_out
  Multiplexer #(.width(3)) multiplexer_3 (
    .in0(ROM1_data[8:6]), .in1(ROM1_data[10:8]), .out(multiplexer_3_out), .sel(Control_Unit1_regsrc_2[2]));
  // Probe on multiplexer_4_out
  Multiplexer #(.width(3)) multiplexer_4 (
    .in0(ROM1_data[2:0]), .in1(ROM1_data[10:8]), .out(multiplexer_4_out), .sel(Control_Unit1_regsrc_2[2]));
  Adder #(.width(32)) adder_2 (.a(adder_1_out), .b(32'h2), .out(adder_2_out));  // open: cin, cout
  Control_Unit Control_Unit1 (
    .Instr(ROM1_data), .ALUFlags(ALU1_aluflags), .MemToReg(Control_Unit1_memtoreg),
    .MemWrite(Control_Unit1_memwrite), .ALUControl(Control_Unit1_alucontrol), .ALUSrc(Control_Unit1_alusrc),
    .ImmSrc(Control_Unit1_immsrc), .RegWrite(Control_Unit1_regwrite),
    .RegSrc({Control_Unit1_regsrc_2[2], Control_Unit1_regsrc}), .PCSrc(Control_Unit1_pcsrc));
  // Probe on Control_Unit1_regwrite
  // Probe on adder_2_out
  // Probe on Control_Unit1_immsrc
  // Probe on Control_Unit1_regsrc
  // RegisterFile RegisterFile1: pin names not known; wires that end beside it: Control_Unit1_regsrc, multiplexer_2_out, multiplexer_3_out, multiplexer_4_out, Control_Unit1_regwrite, RegisterFile1_p6, adder_2_out, RegisterFile1_p8, RegisterFile1_p9
  Immediate Immediate1 (.ImmSrc(Control_Unit1_immsrc), .Instr(ROM1_data), .Imm32(Immediate1_imm32));
  // Probe on Control_Unit1_alusrc
  Multiplexer #(.width(32)) multiplexer_5 (
    .in0(RegisterFile1_p9), .in1(Immediate1_imm32), .out(multiplexer_5_out), .sel(Control_Unit1_alusrc));
  // Probe on Immediate1_imm32
  // Probe on Control_Unit1_alucontrol
  // Probe on RegisterFile1_p8
  // Probe on multiplexer_5_out
  // Probe on RegisterFile1_p9
  // Probe on ALU1_aluflags
  ALU ALU1 (
    .A(RegisterFile1_p8), .B(multiplexer_5_out), .ALUControl(Control_Unit1_alucontrol), .Result(ALU1_result),
    .ALUFlags(ALU1_aluflags));
  // Probe on Control_Unit1_memwrite
  RAM #(.addrWidth(16), .asyncread("true"), .dataWidth(32)) RAM1 (
    .addr(ALU1_result[17:2]), .we(Control_Unit1_memwrite), .clk(clock_2_out), .din(RegisterFile1_p9),
    .dout(RAM1_dout));  // open: oe
  Clock clock_2 (.out(clock_2_out));
  // Probe on ALU1_result
  // Probe on RegisterFile1_p6
  // Probe on Control_Unit1_memtoreg
  // Probe on RAM1_dout
  Multiplexer #(.width(32)) multiplexer_6 (
    .in0(ALU1_result), .in1(RAM1_dout), .out(RegisterFile1_p6), .sel(Control_Unit1_memtoreg));

  // Notes on the sheet:
  //   contents of ROM1 (hex, n*v repeats v):
  //   2111 2222 2333 2444 9101 9202 9303 9404 9904 9a03 9b02 9c01 e7fe
  //   NZCV
endmodule

module CMOS_Gates (
  input  i,
  input  a,
  input  b,
  output o,
  output z
);

  wire transistor_5_out;

  Transistor transistor_1 (.in(1'b1), .out(o), .gate(i));
  Transistor #(.\type ("n")) transistor_2 (.in(1'b0), .out(o), .gate(i));
  Transistor transistor_3 (.in(1'b1), .out(z), .gate(a));
  Transistor #(.\type ("n")) transistor_4 (.in(transistor_5_out), .out(z), .gate(a));
  Transistor #(.\type ("n")) transistor_5 (.in(1'b0), .out(transistor_5_out), .gate(b));
  Transistor transistor_6 (.in(1'b1), .out(z), .gate(b));
endmodule

module Instrcution_Encoder (
  input  [9:0] Opcode,
  output \always ,
  output PCS,
  output MemToReg,
  output MemW,
  output ALUSrc,
  output [1:0] ImmSrc,
  output RegW,
  output [2:0] RegSrc,
  output [2:0] ALUControl,
  output [1:0] FlagW
);

  wire and_3_out, and_4_out, and_5_out, and_6_out, and_7_out, and_10_out, and_11_out, and_12_out, not_2_out,
       not_3_out, not_4_out, not_5_out;

  not not_1 (FlagW[1], Opcode[9]);
  not not_2 (not_2_out, Opcode[8]);
  not not_3 (not_3_out, Opcode[7]);
  not not_4 (not_4_out, Opcode[6]);
  not not_5 (not_5_out, Opcode[5]);
  or or_1 (\always , not_2_out, not_4_out);
  and and_1 (MemToReg, Opcode[9], not_2_out, Opcode[5]);
  and and_2 (MemW, Opcode[9], not_2_out, not_5_out);
  or or_2 (ALUSrc, Opcode[9], Opcode[7]);
  and and_3 (and_3_out, Opcode[9], not_4_out);
  and and_4 (and_4_out, not_2_out, not_3_out);
  and and_5 (and_5_out, not_2_out, Opcode[5]);
  and and_6 (and_6_out, Opcode[9], not_2_out);
  and and_7 (and_7_out, FlagW[1], Opcode[7]);
  and and_8 (RegSrc[1], Opcode[9], not_2_out);
  or or_3 (ALUControl[2], Opcode[6], Opcode[8]);
  and and_9 (ALUControl[1], not_3_out, not_4_out);
  and and_10 (and_10_out, Opcode[7], Opcode[5]);
  and and_11 (and_11_out, not_3_out, not_4_out);
  and and_12 (and_12_out, FlagW[1], not_3_out, Opcode[3]);
  and and_13 (FlagW[0], FlagW[1], Opcode[6]);
  or or_4 (ImmSrc[0], and_3_out, and_4_out);
  or or_5 (RegW, and_5_out, FlagW[1]);
  or or_6 (RegSrc[2], and_6_out, and_7_out);
  or or_7 (ALUControl[0], and_10_out, and_11_out, and_12_out);

  assign ImmSrc[1] = Opcode[8];
  assign PCS = Opcode[8];
  assign RegSrc[0] = Opcode[8];
endmodule
